// Logisim project lab5Dtrigger.circ as structural Verilog: 1 circuit, main circuit main
module main (
  input  in_1,
  output Q,
  output nQ
);

  wire clock_1_out, nand_1_out, nand_2_out, not_1_out, not_2_out;

  Clock clock_1 (.out(clock_1_out));
  not not_1 (not_1_out, in_1);
  not not_2 (not_2_out, clock_1_out);
  nand nand_1 (nand_1_out, not_1_out, in_1, clock_1_out, nand_2_out);
  nand nand_2 (nand_2_out, nand_1_out, clock_1_out);
  nand nand_3 (nQ, nand_1_out, not_2_out, nQ);
  nand nand_4 (nQ, nQ, nand_2_out, not_2_out);

  assign Q = nQ;

  // Notes on the sheet:
  //   D триггер
endmodule
