// Logisim project lab5JKTrigger.circ as structural Verilog: 1 circuit, main circuit main
module main (
  input  C,
  input  J,
  input  K,
  output Q,
  output nQ
);

  wire _3_out, _4_out;

  nand _1 (Q, _3_out, nQ);
  nand _2 (nQ, Q, _4_out, C);
  nand _3 (_3_out, Q, J);
  nand _4 (_4_out, nQ, K);

  // Notes on the sheet:
  //   JK триггер
endmodule
