// Logisim project lab5Ttrigger.circ as structural Verilog: 1 circuit, main circuit main
module main (
  input  D,
  output out_2,
  output out_3
);

  wire C_out, nand_1_out, nand_2_out, nand_3_out, nand_4_out, not_1_out, not_2_out;

  not not_1 (not_1_out, C_out);
  Clock C (.out(C_out));
  not not_2 (not_2_out, C_out);
  nand nand_1 (nand_1_out, D, nand_2_out);
  nand nand_2 (nand_2_out, nand_1_out, not_1_out, C_out);
  nand nand_3 (nand_3_out, D, nand_4_out);
  nand nand_4 (nand_4_out, nand_3_out, C_out, not_2_out);
  nand nand_5 (out_2, nand_2_out, out_3);
  nand nand_6 (out_3, out_2, nand_4_out);

  // Notes on the sheet:
  //   T триггер
endmodule
